// Logisim project COMP_303_FinalProject.circ as structural Verilog: 1 circuit, main circuit main
module main (
);

  wire decoder_1_out0, decoder_1_out1, decoder_1_out2, decoder_1_out3, decoder_1_out4, decoder_1_out5,
       decoder_1_out6, decoder_1_out7, decoder_1_out8, decoder_1_out9, decoder_1_out10, decoder_1_out11,
       decoder_1_out12, decoder_1_out13, decoder_1_out14, decoder_1_out15, undriven_2, undriven_3, undriven_4;
  wire [15:0] multiplexer_1_out, multiplexer_2_out, reg0_q, reg1_q, reg2_q, reg3_q, register_1_q,
       register_2_q, register_3_q, register_4_q, register_5_q, register_6_q, register_7_q, register_8_q,
       register_9_q, register_10_q, register_11_q, register_12_q, undriven;

  // Full_Adder full_adder_1: pin names not known
  Decoder #(.select(4)) decoder_1 (
    .out0(decoder_1_out0), .out1(decoder_1_out1), .out2(decoder_1_out2), .out3(decoder_1_out3),
    .out4(decoder_1_out4), .out5(decoder_1_out5), .out6(decoder_1_out6), .out7(decoder_1_out7),
    .out8(decoder_1_out8), .out9(decoder_1_out9), .out10(decoder_1_out10), .out11(decoder_1_out11),
    .out12(decoder_1_out12), .out13(decoder_1_out13), .out14(decoder_1_out14), .out15(decoder_1_out15),
    .en(undriven_2));  // open: sel
  Register #(.width(16)) reg0 (.D(undriven), .Q(reg0_q), .clk(decoder_1_out0));  // open: en, clr
  Register #(.width(16)) register_1 (.D(undriven), .Q(register_1_q), .clk(decoder_1_out4));  // open: en, clr
  Register #(.width(16)) register_2 (.D(undriven), .Q(register_2_q), .clk(decoder_1_out8));  // open: en, clr
  Register #(.width(16)) register_3 (.D(undriven), .Q(register_3_q), .clk(decoder_1_out12));  // open: en, clr
  Register #(.width(16)) reg1 (.D(undriven), .Q(reg1_q), .clk(decoder_1_out1));  // open: en, clr
  Register #(.width(16)) register_4 (.D(undriven), .Q(register_4_q), .clk(decoder_1_out5));  // open: en, clr
  Register #(.width(16)) register_5 (.D(undriven), .Q(register_5_q), .clk(decoder_1_out9));  // open: en, clr
  Register #(.width(16)) register_6 (.D(undriven), .Q(register_6_q), .clk(decoder_1_out13));  // open: en, clr
  Register #(.width(16)) reg2 (.D(undriven), .Q(reg2_q), .clk(decoder_1_out2));  // open: en, clr
  Register #(.width(16)) register_7 (.D(undriven), .Q(register_7_q), .clk(decoder_1_out6));  // open: en, clr
  Register #(.width(16)) register_8 (.D(undriven), .Q(register_8_q), .clk(decoder_1_out10));  // open: en, clr
  Register #(.width(16)) register_9 (.D(undriven), .Q(register_9_q), .clk(decoder_1_out14));  // open: en, clr
  Register #(.width(16)) reg3 (.D(undriven), .Q(reg3_q), .clk(decoder_1_out3));  // open: en, clr
  Register #(.width(16)) register_10 (.D(undriven), .Q(register_10_q), .clk(decoder_1_out7));  // open: en, clr
  Register #(.width(16)) register_11 (.D(undriven), .Q(register_11_q), .clk(decoder_1_out11));  // open: en, clr
  Register #(.width(16)) register_12 (.D(undriven), .Q(register_12_q), .clk(decoder_1_out15));  // open: en, clr
  Multiplexer #(.select(4), .width(16)) multiplexer_1 (
    .in0(reg0_q), .in1(reg1_q), .in2(reg2_q), .in3(reg3_q), .in4(register_1_q), .in5(register_4_q),
    .in6(register_7_q), .in7(register_10_q), .in8(register_2_q), .in9(register_5_q), .in10(register_8_q),
    .in11(register_11_q), .in12(register_3_q), .in13(register_6_q), .in14(register_9_q),
    .in15(register_12_q), .out(multiplexer_1_out), .en(undriven_3));  // open: sel
  Multiplexer #(.select(4), .width(16)) multiplexer_2 (
    .in0(reg0_q), .in1(reg1_q), .in2(reg2_q), .in3(reg3_q), .in4(register_1_q), .in5(register_4_q),
    .in6(register_7_q), .in7(register_10_q), .in8(register_2_q), .in9(register_5_q), .in10(register_8_q),
    .in11(register_11_q), .in12(register_3_q), .in13(register_6_q), .in14(register_9_q),
    .in15(register_12_q), .out(multiplexer_2_out), .en(undriven_4));  // open: sel

  // Notes on the sheet:
  //   WriteData
  //   WriteAddr
  //   ReadAddr1
  //   ReadAddr2
  //   ReadData1
  //   ReadData2
endmodule
